// Logisim project main.circ as structural Verilog: 2 circuits, main circuit main
module main (
);

  wire and_4_out, and_5_out, and_6_out, and_7_out, and_8_out, and_9_out, and_10_out, button_2_out,
       button_3_out, button_4_out, button_5_out, button_6_out, button_7_out, button_8_out,
       button_driver_1_trigger, button_register, c, cdm_8_1_p2, cdm_8_1_p4, cdm_8_1_p5, cdm_8_1_p6,
       cdm_8_1_p7, cdm_8_1_p8, cdm_8_1_p9, cdm_8_1_p10, cdm_8_1_p11, cl, clear_button_register, code,
       comparator_4_eq, comparator_5_eq, comparator_6_eq, comparator_7_eq, comparator_8_eq, comparator_9_eq,
       Computing, data, display_driver_rev2_2_cl_2, display_driver_rev2_2_r_w_2,
       display_driver_rev2_2_reset_2, display_driver_rev2_3_cl_2, display_driver_rev2_3_r_w_2,
       display_driver_rev2_3_reset_2, display_driver_rev2_4_cl_2, display_driver_rev2_4_r_w_2,
       display_driver_rev2_4_reset_2, display_driver_rev2_5_cl_2, display_driver_rev2_5_r_w_2,
       display_driver_rev2_5_reset_2, display_driver_rev2_6_cl_2, display_driver_rev2_6_r_w_2,
       display_driver_rev2_6_reset_2, display_driver_rev2_7_cl_2, display_driver_rev2_7_r_w_2,
       display_driver_rev2_7_reset_2, display_driver_rev2_8_cl_2, display_driver_rev2_8_r_w_2,
       display_driver_rev2_8_reset_2, display_driver_rev2_9_cl_2, display_driver_rev2_9_r_w_2,
       display_driver_rev2_9_reset_2, display_driver_rev2_10_cl_2, display_driver_rev2_10_r_w_2,
       display_driver_rev2_10_reset_2, display_driver_rev2_11_cl_2, display_driver_rev2_11_r_w_2,
       display_driver_rev2_11_reset_2, display_driver_rev2_12_cl_2, display_driver_rev2_12_r_w_2,
       display_driver_rev2_12_reset_2, display_driver_rev2_13_cl_2, display_driver_rev2_13_r_w_2,
       display_driver_rev2_13_reset_2, display_driver_rev2_14_cl_2, display_driver_rev2_14_r_w_2,
       display_driver_rev2_14_reset_2, Error, ext_register_2_cl_2, ext_register_2_data_flag_out,
       ext_register_2_r_w_prime_out, ext_register_2_reset_2, ext_register_3_cl_2,
       ext_register_3_data_flag_out, ext_register_3_r_w_prime_out, ext_register_3_reset_2, Game_stopped, h,
       Initializing_memory, IO_op, not_1_out, not_2_out, not_3_out, or_1_out, pull_resistor_1_node,
       pull_resistor_2_node, pull_resistor_3_node, pull_resistor_6_node, pull_resistor_7_node,
       r_w_flag_field, rand_char, Ready, res_CPU, W_R_to_from_field, Waiting_user_action, wl_read;
  wire [0:0] or_2_out;
  wire [3:0] addr_field, button_driver_1_addr_2, button_driver_2_addr_2, button_driver_3_addr_2,
       button_driver_4_addr_2, button_driver_5_addr_2, button_driver_6_addr_2, button_driver_7_addr_2,
       display_driver_rev2_1_bcd_1, display_driver_rev2_1_bcd_2, display_driver_rev2_2_add_for_button_driver,
       display_driver_rev2_2_addr_out, display_driver_rev2_2_addr_out_chain, display_driver_rev2_2_bcd_1,
       display_driver_rev2_2_bcd_2, display_driver_rev2_3_addr_out, display_driver_rev2_3_addr_out_chain,
       display_driver_rev2_3_bcd_1, display_driver_rev2_3_bcd_2, display_driver_rev2_4_add_for_button_driver,
       display_driver_rev2_4_addr_out, display_driver_rev2_4_addr_out_chain, display_driver_rev2_4_bcd_1,
       display_driver_rev2_4_bcd_2, display_driver_rev2_5_addr_out, display_driver_rev2_5_addr_out_chain,
       display_driver_rev2_5_bcd_1, display_driver_rev2_5_bcd_2, display_driver_rev2_6_add_for_button_driver,
       display_driver_rev2_6_addr_out, display_driver_rev2_6_addr_out_chain, display_driver_rev2_6_bcd_1,
       display_driver_rev2_6_bcd_2, display_driver_rev2_7_addr_out, display_driver_rev2_7_addr_out_chain,
       display_driver_rev2_7_bcd_1, display_driver_rev2_7_bcd_2, display_driver_rev2_8_add_for_button_driver,
       display_driver_rev2_8_addr_out, display_driver_rev2_8_addr_out_chain, display_driver_rev2_8_bcd_1,
       display_driver_rev2_8_bcd_2, display_driver_rev2_9_addr_out, display_driver_rev2_9_addr_out_chain,
       display_driver_rev2_9_bcd_1, display_driver_rev2_9_bcd_2,
       display_driver_rev2_10_add_for_button_driver, display_driver_rev2_10_addr_out,
       display_driver_rev2_10_addr_out_chain, display_driver_rev2_10_bcd_1, display_driver_rev2_10_bcd_2,
       display_driver_rev2_11_addr_out, display_driver_rev2_11_addr_out_chain, display_driver_rev2_11_bcd_1,
       display_driver_rev2_11_bcd_2, display_driver_rev2_12_add_for_button_driver,
       display_driver_rev2_12_addr_out, display_driver_rev2_12_addr_out_chain, display_driver_rev2_12_bcd_1,
       display_driver_rev2_12_bcd_2, display_driver_rev2_13_add_for_button_driver,
       display_driver_rev2_13_addr_out, display_driver_rev2_13_addr_out_chain, display_driver_rev2_13_bcd_1,
       display_driver_rev2_13_bcd_2, display_driver_rev2_14_addr_out, display_driver_rev2_14_addr_out_chain,
       display_driver_rev2_14_bcd_1, display_driver_rev2_14_bcd_2, incrementer_1_out_2;
  wire [7:0] bank_addr_number, cdm_8_1_p14, cdm_8_1_p15, cdm_addr, data_to_field_write,
       display_driver_rev2_2_data_out, display_driver_rev2_3_data_out, display_driver_rev2_4_data_out,
       display_driver_rev2_5_data_out, display_driver_rev2_6_data_out, display_driver_rev2_7_data_out,
       display_driver_rev2_8_data_out, display_driver_rev2_9_data_out, display_driver_rev2_10_data_out,
       display_driver_rev2_11_data_out, display_driver_rev2_12_data_out, display_driver_rev2_13_data_out,
       display_driver_rev2_14_data_out, ext_register_2_cpu_mem_addr_out, ext_register_2_io_out,
       ext_register_3_cpu_mem_addr_out, ext_register_3_io_out, IO, random_1_out, register_2_q;
  wire [7:5] ext_register_2_data_out;

  ext_register ext_register_1 (
    .register_addres(8'hf), .cpu_mem_addr_in(ext_register_2_cpu_mem_addr_out),
    .r_w_prime(ext_register_2_r_w_prime_out), .data_flag_in(ext_register_2_data_flag_out),
    .IO_in(ext_register_2_io_out), .cl(ext_register_2_cl_2), .reset(ext_register_2_reset_2),
    .data_out({Ready, clear_button_register, Initializing_memory, Game_stopped, Waiting_user_action, Computing, W_R_to_from_field, Error}));  // open: cpu_mem_addr_out, r_w_prime_out, data_flag_out, IO_out, cl_2, reset_2
  ext_register ext_register_2 (
    .register_addres(8'hfc), .cpu_mem_addr_out(ext_register_2_cpu_mem_addr_out),
    .r_w_prime_out(ext_register_2_r_w_prime_out), .data_flag_out(ext_register_2_data_flag_out),
    .IO_out(ext_register_2_io_out), .cl_2(ext_register_2_cl_2), .reset_2(ext_register_2_reset_2),
    .cpu_mem_addr_in(ext_register_3_cpu_mem_addr_out), .r_w_prime(ext_register_3_r_w_prime_out),
    .data_flag_in(ext_register_3_data_flag_out), .IO_in(ext_register_3_io_out), .cl(ext_register_3_cl_2),
    .reset(ext_register_3_reset_2), .data_out({ext_register_2_data_out, r_w_flag_field, addr_field}));
  ext_register ext_register_3 (
    .register_addres(8'hfe), .cpu_mem_addr_out(ext_register_3_cpu_mem_addr_out),
    .r_w_prime_out(ext_register_3_r_w_prime_out), .data_flag_out(ext_register_3_data_flag_out),
    .IO_out(ext_register_3_io_out), .cl_2(ext_register_3_cl_2), .reset_2(ext_register_3_reset_2),
    .cpu_mem_addr_in(cdm_addr), .r_w_prime(IO_op), .data_flag_in(data), .IO_in(IO), .cl(cl), .reset(res_CPU),
    .data_out(data_to_field_write));
  // Probe on data_to_field_write
  Pull_Resistor pull_resistor_1 (.node(pull_resistor_1_node));
  Comparator #(.mode("unsigned")) comparator_1 (.a(8'hf9), .b(cdm_addr), .eq(pull_resistor_1_node));  // open: gt, lt
  Pull_Resistor pull_resistor_2 (.node(pull_resistor_2_node));
  Comparator #(.mode("unsigned")) comparator_2 (.a(8'hfa), .b(cdm_addr), .eq(pull_resistor_2_node));  // open: gt, lt
  Pull_Resistor pull_resistor_3 (.node(pull_resistor_3_node));
  Comparator #(.mode("unsigned")) comparator_3 (.a(8'hf8), .b(cdm_addr), .eq(pull_resistor_3_node));  // open: gt, lt
  // Probe on cdm_8_1_p2
  Clock clock_1 (.out(cl));
  Button button_1 (.out(res_CPU));
  Comparator comparator_4 (.a(cdm_addr), .b({8{1'b1}}), .eq(comparator_4_eq));  // open: gt, lt
  not not_1 (not_1_out, IO_op);
  // Probe on addr_field
  Pull_Resistor pull_resistor_4 (.node(button_register));
  and and_1 (button_register, pull_resistor_1_node, data);
  and and_2 (rand_char, pull_resistor_2_node, data);
  and and_3 (wl_read, pull_resistor_3_node, data);
  Random #(.seed(5)) random_1 (.clk(cl), .next(rand_char), .out(random_1_out), .clr(res_CPU));
  // Probe on cdm_8_1_p6
  // Probe on cdm_8_1_p5
  // Probe on cdm_8_1_p4
  and and_4 (and_4_out, comparator_4_eq, data, not_1_out);
  assign IO = rand_char ? random_1_out : 8'bz;  // Controlled_Buffer controlled_buffer_1
  // Probe on cdm_8_1_p9
  // Probe on cdm_8_1_p8
  // Probe on cdm_8_1_p7
  Register register_1 (.D(IO), .en(and_4_out), .Q(bank_addr_number), .clk(cl), .clr(res_CPU));
  // CdM_8 cdm_8_1: pin names not known; wires that end beside it: cl, cdm_8_1_p2, res_CPU, cdm_8_1_p4, cdm_8_1_p5, cdm_8_1_p6, cdm_8_1_p7, cdm_8_1_p8, cdm_8_1_p9, cdm_8_1_p10, cdm_8_1_p11, IO_op, cdm_addr, cdm_8_1_p14, cdm_8_1_p15
  Decoder #(.disabled(0)) decoder_1 (.out0(code), .out1(data), .sel(cdm_8_1_p10), .en(cdm_8_1_p11));
  assign IO = not_2_out ? cdm_8_1_p14 : 8'bz;  // Controlled_Buffer controlled_buffer_2
  not not_2 (not_2_out, IO_op);
  assign cdm_8_1_p15 = IO_op ? IO : 8'bz;  // Controlled_Buffer controlled_buffer_3
  and and_5 (and_5_out, data, ~rand_char, ~button_register, ~wl_read);  // AND_Gate
  Comparator comparator_5 (.a({8{1'b0}}), .b(bank_addr_number), .eq(comparator_5_eq));  // open: gt, lt
  Comparator comparator_6 (.a(8'h1), .b(bank_addr_number), .eq(comparator_6_eq));  // open: gt, lt
  Comparator comparator_7 (.a(8'h2), .b(bank_addr_number), .eq(comparator_7_eq));  // open: gt, lt
  Comparator comparator_8 (.a(8'h3), .b(bank_addr_number), .eq(comparator_8_eq));  // open: gt, lt
  Comparator comparator_9 (.a(8'h4), .b(bank_addr_number), .eq(comparator_9_eq));  // open: gt, lt
  and and_6 (and_6_out, comparator_5_eq, code);
  and and_7 (and_7_out, comparator_6_eq, code);
  and and_8 (and_8_out, comparator_7_eq, code);
  and and_9 (and_9_out, comparator_8_eq, code);
  and and_10 (and_10_out, comparator_9_eq, code);
  RAM ram_1 (.addr(cdm_addr), .data(IO), .sel(and_5_out), .clk(cl), .ld(IO_op), .clr(res_CPU));
  ROM rom_1 (.addr(cdm_addr), .data(IO), .sel(and_6_out));
  ROM rom_2 (.addr(cdm_addr), .data(IO), .sel(and_7_out));
  ROM rom_3 (.addr(cdm_addr), .data(IO), .sel(and_8_out));
  ROM rom_4 (.addr(cdm_addr), .data(IO), .sel(and_9_out));
  ROM rom_5 (.addr(cdm_addr), .data(IO), .sel(and_10_out));
  or or_1 (or_1_out, res_CPU, clear_button_register);
  display_driver_rev2 display_driver_rev2_1 (
    .addr_in(display_driver_rev2_2_addr_out), .addr_in_chain(display_driver_rev2_2_addr_out_chain),
    .data(display_driver_rev2_2_data_out), .cl(display_driver_rev2_2_cl_2),
    .bcd_1(display_driver_rev2_1_bcd_1), .bcd_2(display_driver_rev2_1_bcd_2),
    .r_w(display_driver_rev2_2_r_w_2), .reset(display_driver_rev2_2_reset_2));  // open: addr_out, addr_out_chain, data_out, cl_2, is_0, r_w_2, reset_2, add_for_button_driver
  LED led_1 (.in(c));
  Pull_Resistor pull_resistor_5 (.node(c));
  assign IO = button_register ? register_2_q : 8'bz;  // Controlled_Buffer controlled_buffer_4
  Register register_2 (
    .D({4'b0000, button_driver_1_addr_2}), .en(not_3_out), .Q(register_2_q), .clk(cl), .clr(or_1_out));
  Hex_Digit_Display hex_digit_display_1 (.value(display_driver_rev2_1_bcd_2));  // open: dp
  Hex_Digit_Display hex_digit_display_2 (.value(display_driver_rev2_1_bcd_1));  // open: dp
  WLD wld_1 (
    .in_3(pull_resistor_6_node), .des(display_driver_rev2_1_bcd_1), .ed(display_driver_rev2_1_bcd_2),
    .win(c), .lose(h));
  not not_3 (not_3_out, button_driver_1_trigger);
  assign IO = wl_read ? {{7{1'b0}}, or_2_out[0]} : 8'bz;  // Controlled_Buffer controlled_buffer_5
  Pull_Resistor #(.pull(1)) pull_resistor_6 (.node(pull_resistor_6_node));
  display_driver_rev2 display_driver_rev2_2 (
    .addr_in(display_driver_rev2_3_addr_out), .addr_in_chain(display_driver_rev2_3_addr_out_chain),
    .data(display_driver_rev2_3_data_out), .cl(display_driver_rev2_3_cl_2),
    .addr_out(display_driver_rev2_2_addr_out), .addr_out_chain(display_driver_rev2_2_addr_out_chain),
    .data_out(display_driver_rev2_2_data_out), .cl_2(display_driver_rev2_2_cl_2),
    .bcd_1(display_driver_rev2_2_bcd_1), .bcd_2(display_driver_rev2_2_bcd_2), .is_0(pull_resistor_6_node),
    .r_w(display_driver_rev2_3_r_w_2), .r_w_2(display_driver_rev2_2_r_w_2),
    .reset(display_driver_rev2_3_reset_2), .reset_2(display_driver_rev2_2_reset_2),
    .add_for_button_driver(display_driver_rev2_2_add_for_button_driver));
  Hex_Digit_Display hex_digit_display_3 (.value(display_driver_rev2_2_bcd_1));  // open: dp
  LED err (.in(Error));
  LED err_2 (.in(Error));
  LED err_3 (.in(Error));
  Pull_Resistor #(.pull(1)) pull_resistor_7 (.node(pull_resistor_7_node));
  Hex_Digit_Display hex_digit_display_4 (.value(display_driver_rev2_4_bcd_1));  // open: dp
  Hex_Digit_Display hex_digit_display_5 (.value(display_driver_rev2_4_bcd_2));  // open: dp
  button_driver button_driver_1 (
    .addr_2(button_driver_1_addr_2), .pos(display_driver_rev2_4_add_for_button_driver),
    .button(button_2_out), .trigger(button_driver_1_trigger), .addr(button_driver_3_addr_2));
  Button button_2 (.out(button_2_out));
  or or_2 (or_2_out[0], c, h);
  Button button_3 (.out(button_3_out));
  button_driver button_driver_2 (
    .addr_2(button_driver_2_addr_2), .pos(display_driver_rev2_2_add_for_button_driver),
    .button(button_3_out), .trigger(button_driver_1_trigger));  // open: addr
  display_driver_rev2 display_driver_rev2_3 (
    .addr_in(display_driver_rev2_5_addr_out), .addr_in_chain(display_driver_rev2_5_addr_out_chain),
    .data(display_driver_rev2_5_data_out), .cl(display_driver_rev2_5_cl_2),
    .addr_out(display_driver_rev2_3_addr_out), .addr_out_chain(display_driver_rev2_3_addr_out_chain),
    .data_out(display_driver_rev2_3_data_out), .cl_2(display_driver_rev2_3_cl_2),
    .bcd_1(display_driver_rev2_3_bcd_1), .bcd_2(display_driver_rev2_3_bcd_2), .is_0(pull_resistor_6_node),
    .r_w(display_driver_rev2_5_r_w_2), .r_w_2(display_driver_rev2_3_r_w_2),
    .reset(display_driver_rev2_5_reset_2), .reset_2(display_driver_rev2_3_reset_2));  // open: add_for_button_driver
  Hex_Digit_Display hex_digit_display_6 (.value(display_driver_rev2_2_bcd_2));  // open: dp
  LED field_IO (.in(W_R_to_from_field));
  Hex_Digit_Display hex_digit_display_7 (.value(display_driver_rev2_6_bcd_1));  // open: dp
  display_driver_rev2 display_driver_rev2_4 (
    .addr_in(addr_field), .addr_in_chain(4'b0000), .data(data_to_field_write), .cl(cl),
    .addr_out(display_driver_rev2_4_addr_out), .addr_out_chain(display_driver_rev2_4_addr_out_chain),
    .data_out(display_driver_rev2_4_data_out), .cl_2(display_driver_rev2_4_cl_2),
    .bcd_1(display_driver_rev2_4_bcd_1), .bcd_2(display_driver_rev2_4_bcd_2), .is_0(pull_resistor_7_node),
    .r_w(r_w_flag_field), .r_w_2(display_driver_rev2_4_r_w_2), .reset(res_CPU),
    .reset_2(display_driver_rev2_4_reset_2),
    .add_for_button_driver(display_driver_rev2_4_add_for_button_driver));
  Hex_Digit_Display hex_digit_display_8 (.value(display_driver_rev2_3_bcd_2));  // open: dp
  Hex_Digit_Display hex_digit_display_9 (.value(display_driver_rev2_3_bcd_1));  // open: dp
  LED u_computing (.in(Computing));
  Hex_Digit_Display hex_digit_display_10 (.value(display_driver_rev2_6_bcd_2));  // open: dp
  button_driver button_driver_3 (
    .addr_2(button_driver_3_addr_2), .pos(display_driver_rev2_6_add_for_button_driver),
    .button(button_4_out), .trigger(button_driver_1_trigger), .addr(button_driver_4_addr_2));
  Button button_4 (.out(button_4_out));
  display_driver_rev2 display_driver_rev2_5 (
    .addr_in(display_driver_rev2_7_addr_out), .addr_in_chain(display_driver_rev2_7_addr_out_chain),
    .data(display_driver_rev2_7_data_out), .cl(display_driver_rev2_7_cl_2),
    .addr_out(display_driver_rev2_5_addr_out), .addr_out_chain(display_driver_rev2_5_addr_out_chain),
    .data_out(display_driver_rev2_5_data_out), .cl_2(display_driver_rev2_5_cl_2),
    .bcd_1(display_driver_rev2_5_bcd_1), .bcd_2(display_driver_rev2_5_bcd_2), .is_0(pull_resistor_6_node),
    .r_w(display_driver_rev2_7_r_w_2), .r_w_2(display_driver_rev2_5_r_w_2),
    .reset(display_driver_rev2_7_reset_2), .reset_2(display_driver_rev2_5_reset_2));  // open: add_for_button_driver
  LED Waiting_user (.in(Waiting_user_action));
  Hex_Digit_Display hex_digit_display_11 (.value(display_driver_rev2_8_bcd_1));  // open: dp
  Hex_Digit_Display hex_digit_display_12 (.value(display_driver_rev2_8_bcd_2));  // open: dp
  display_driver_rev2 display_driver_rev2_6 (
    .addr_in(display_driver_rev2_4_addr_out), .addr_in_chain(display_driver_rev2_4_addr_out_chain),
    .data(display_driver_rev2_4_data_out), .cl(display_driver_rev2_4_cl_2),
    .addr_out(display_driver_rev2_6_addr_out), .addr_out_chain(display_driver_rev2_6_addr_out_chain),
    .data_out(display_driver_rev2_6_data_out), .cl_2(display_driver_rev2_6_cl_2),
    .bcd_1(display_driver_rev2_6_bcd_1), .bcd_2(display_driver_rev2_6_bcd_2), .is_0(pull_resistor_7_node),
    .r_w(display_driver_rev2_4_r_w_2), .r_w_2(display_driver_rev2_6_r_w_2),
    .reset(display_driver_rev2_4_reset_2), .reset_2(display_driver_rev2_6_reset_2),
    .add_for_button_driver(display_driver_rev2_6_add_for_button_driver));
  Button button_5 (.out(button_5_out));
  display_driver_rev2 display_driver_rev2_7 (
    .addr_in(display_driver_rev2_9_addr_out), .addr_in_chain(display_driver_rev2_9_addr_out_chain),
    .data(display_driver_rev2_9_data_out), .cl(display_driver_rev2_9_cl_2),
    .addr_out(display_driver_rev2_7_addr_out), .addr_out_chain(display_driver_rev2_7_addr_out_chain),
    .data_out(display_driver_rev2_7_data_out), .cl_2(display_driver_rev2_7_cl_2),
    .bcd_1(display_driver_rev2_7_bcd_1), .bcd_2(display_driver_rev2_7_bcd_2), .is_0(pull_resistor_6_node),
    .r_w(display_driver_rev2_9_r_w_2), .r_w_2(display_driver_rev2_7_r_w_2),
    .reset(display_driver_rev2_9_reset_2), .reset_2(display_driver_rev2_7_reset_2));  // open: add_for_button_driver
  Hex_Digit_Display hex_digit_display_13 (.value(display_driver_rev2_5_bcd_2));  // open: dp
  Hex_Digit_Display hex_digit_display_14 (.value(display_driver_rev2_5_bcd_1));  // open: dp
  LED END_OF_GAME (.in(Game_stopped));
  LED led_2 (.in(Game_stopped));
  LED led_3 (.in(Game_stopped));
  Hex_Digit_Display hex_digit_display_15 (.value(display_driver_rev2_10_bcd_1));  // open: dp
  display_driver_rev2 display_driver_rev2_8 (
    .addr_in(display_driver_rev2_6_addr_out), .addr_in_chain(display_driver_rev2_6_addr_out_chain),
    .data(display_driver_rev2_6_data_out), .cl(display_driver_rev2_6_cl_2),
    .addr_out(display_driver_rev2_8_addr_out), .addr_out_chain(display_driver_rev2_8_addr_out_chain),
    .data_out(display_driver_rev2_8_data_out), .cl_2(display_driver_rev2_8_cl_2),
    .bcd_1(display_driver_rev2_8_bcd_1), .bcd_2(display_driver_rev2_8_bcd_2), .is_0(pull_resistor_7_node),
    .r_w(display_driver_rev2_6_r_w_2), .r_w_2(display_driver_rev2_8_r_w_2),
    .reset(display_driver_rev2_6_reset_2), .reset_2(display_driver_rev2_8_reset_2),
    .add_for_button_driver(display_driver_rev2_8_add_for_button_driver));
  button_driver button_driver_4 (
    .addr_2(button_driver_4_addr_2), .pos(display_driver_rev2_8_add_for_button_driver),
    .button(button_5_out), .trigger(button_driver_1_trigger), .addr(button_driver_5_addr_2));
  Hex_Digit_Display hex_digit_display_16 (.value(display_driver_rev2_7_bcd_1));  // open: dp
  LED init_memory (.in(Initializing_memory));
  Hex_Digit_Display hex_digit_display_17 (.value(display_driver_rev2_10_bcd_2));  // open: dp
  button_driver button_driver_5 (
    .addr_2(button_driver_5_addr_2), .pos(display_driver_rev2_10_add_for_button_driver),
    .button(button_6_out), .trigger(button_driver_1_trigger), .addr(button_driver_6_addr_2));
  Button button_6 (.out(button_6_out));
  display_driver_rev2 display_driver_rev2_9 (
    .addr_in(display_driver_rev2_11_addr_out), .addr_in_chain(display_driver_rev2_11_addr_out_chain),
    .data(display_driver_rev2_11_data_out), .cl(display_driver_rev2_11_cl_2),
    .addr_out(display_driver_rev2_9_addr_out), .addr_out_chain(display_driver_rev2_9_addr_out_chain),
    .data_out(display_driver_rev2_9_data_out), .cl_2(display_driver_rev2_9_cl_2),
    .bcd_1(display_driver_rev2_9_bcd_1), .bcd_2(display_driver_rev2_9_bcd_2), .is_0(pull_resistor_6_node),
    .r_w(display_driver_rev2_11_r_w_2), .r_w_2(display_driver_rev2_9_r_w_2),
    .reset(display_driver_rev2_11_reset_2), .reset_2(display_driver_rev2_9_reset_2));  // open: add_for_button_driver
  Hex_Digit_Display hex_digit_display_18 (.value(display_driver_rev2_7_bcd_2));  // open: dp
  Hex_Digit_Display hex_digit_display_19 (.value(display_driver_rev2_12_bcd_1));  // open: dp
  display_driver_rev2 display_driver_rev2_10 (
    .addr_in(display_driver_rev2_8_addr_out), .addr_in_chain(display_driver_rev2_8_addr_out_chain),
    .data(display_driver_rev2_8_data_out), .cl(display_driver_rev2_8_cl_2),
    .addr_out(display_driver_rev2_10_addr_out), .addr_out_chain(display_driver_rev2_10_addr_out_chain),
    .data_out(display_driver_rev2_10_data_out), .cl_2(display_driver_rev2_10_cl_2),
    .bcd_1(display_driver_rev2_10_bcd_1), .bcd_2(display_driver_rev2_10_bcd_2), .is_0(pull_resistor_7_node),
    .r_w(display_driver_rev2_8_r_w_2), .r_w_2(display_driver_rev2_10_r_w_2),
    .reset(display_driver_rev2_8_reset_2), .reset_2(display_driver_rev2_10_reset_2),
    .add_for_button_driver(display_driver_rev2_10_add_for_button_driver));
  Hex_Digit_Display hex_digit_display_20 (.value(display_driver_rev2_9_bcd_1));  // open: dp
  Hex_Digit_Display hex_digit_display_21 (.value(display_driver_rev2_9_bcd_2));  // open: dp
  LED u_ready (.in(Ready));
  Hex_Digit_Display hex_digit_display_22 (.value(display_driver_rev2_12_bcd_2));  // open: dp
  button_driver button_driver_6 (
    .addr_2(button_driver_6_addr_2), .pos(display_driver_rev2_12_add_for_button_driver),
    .button(button_7_out), .trigger(button_driver_1_trigger), .addr(button_driver_7_addr_2));
  Button button_7 (.out(button_7_out));
  display_driver_rev2 display_driver_rev2_11 (
    .addr_in(display_driver_rev2_14_addr_out), .addr_in_chain(incrementer_1_out_2),
    .data(display_driver_rev2_14_data_out), .cl(display_driver_rev2_14_cl_2),
    .addr_out(display_driver_rev2_11_addr_out), .addr_out_chain(display_driver_rev2_11_addr_out_chain),
    .data_out(display_driver_rev2_11_data_out), .cl_2(display_driver_rev2_11_cl_2),
    .bcd_1(display_driver_rev2_11_bcd_1), .bcd_2(display_driver_rev2_11_bcd_2), .is_0(pull_resistor_6_node),
    .r_w(display_driver_rev2_14_r_w_2), .r_w_2(display_driver_rev2_11_r_w_2),
    .reset(display_driver_rev2_14_reset_2), .reset_2(display_driver_rev2_11_reset_2));  // open: add_for_button_driver
  Hex_Digit_Display hex_digit_display_23 (.value(display_driver_rev2_11_bcd_1));  // open: dp
  Hex_Digit_Display hex_digit_display_24 (.value(display_driver_rev2_13_bcd_2));  // open: dp
  Hex_Digit_Display hex_digit_display_25 (.value(display_driver_rev2_13_bcd_1));  // open: dp
  display_driver_rev2 display_driver_rev2_12 (
    .addr_in(display_driver_rev2_10_addr_out), .addr_in_chain(display_driver_rev2_10_addr_out_chain),
    .data(display_driver_rev2_10_data_out), .cl(display_driver_rev2_10_cl_2),
    .addr_out(display_driver_rev2_12_addr_out), .addr_out_chain(display_driver_rev2_12_addr_out_chain),
    .data_out(display_driver_rev2_12_data_out), .cl_2(display_driver_rev2_12_cl_2),
    .bcd_1(display_driver_rev2_12_bcd_1), .bcd_2(display_driver_rev2_12_bcd_2), .is_0(pull_resistor_7_node),
    .r_w(display_driver_rev2_10_r_w_2), .r_w_2(display_driver_rev2_12_r_w_2),
    .reset(display_driver_rev2_10_reset_2), .reset_2(display_driver_rev2_12_reset_2),
    .add_for_button_driver(display_driver_rev2_12_add_for_button_driver));
  Button button_8 (.out(button_8_out));
  Hex_Digit_Display hex_digit_display_26 (.value(display_driver_rev2_11_bcd_2));  // open: dp
  WLD wld_2 (
    .in_3(pull_resistor_7_node), .des(display_driver_rev2_14_bcd_1), .ed(display_driver_rev2_14_bcd_2),
    .win(h), .lose(c));
  display_driver_rev2 display_driver_rev2_13 (
    .addr_in(display_driver_rev2_12_addr_out), .addr_in_chain(display_driver_rev2_12_addr_out_chain),
    .data(display_driver_rev2_12_data_out), .cl(display_driver_rev2_12_cl_2),
    .addr_out(display_driver_rev2_13_addr_out), .addr_out_chain(display_driver_rev2_13_addr_out_chain),
    .data_out(display_driver_rev2_13_data_out), .cl_2(display_driver_rev2_13_cl_2),
    .bcd_1(display_driver_rev2_13_bcd_1), .bcd_2(display_driver_rev2_13_bcd_2), .is_0(pull_resistor_7_node),
    .r_w(display_driver_rev2_12_r_w_2), .r_w_2(display_driver_rev2_13_r_w_2),
    .reset(display_driver_rev2_12_reset_2), .reset_2(display_driver_rev2_13_reset_2),
    .add_for_button_driver(display_driver_rev2_13_add_for_button_driver));
  button_driver button_driver_7 (
    .addr_2(button_driver_7_addr_2), .pos(display_driver_rev2_13_add_for_button_driver),
    .button(button_8_out), .trigger(button_driver_1_trigger), .addr(button_driver_2_addr_2));
  Pull_Resistor #(.pull(1)) pull_resistor_8 (.node(button_driver_1_trigger));
  Hex_Digit_Display hex_digit_display_27 (.value(display_driver_rev2_14_bcd_1));  // open: dp
  incrementer incrementer_1 (.in_1(display_driver_rev2_14_addr_out_chain), .out_2(incrementer_1_out_2));
  Hex_Digit_Display hex_digit_display_28 (.value(display_driver_rev2_14_bcd_2));  // open: dp
  LED led_4 (.in(h));
  Pull_Resistor pull_resistor_9 (.node(h));
  display_driver_rev2 display_driver_rev2_14 (
    .addr_in(display_driver_rev2_13_addr_out), .addr_in_chain(display_driver_rev2_13_addr_out_chain),
    .data(display_driver_rev2_13_data_out), .cl(display_driver_rev2_13_cl_2),
    .addr_out(display_driver_rev2_14_addr_out), .addr_out_chain(display_driver_rev2_14_addr_out_chain),
    .data_out(display_driver_rev2_14_data_out), .cl_2(display_driver_rev2_14_cl_2),
    .bcd_1(display_driver_rev2_14_bcd_1), .bcd_2(display_driver_rev2_14_bcd_2),
    .r_w(display_driver_rev2_13_r_w_2), .r_w_2(display_driver_rev2_14_r_w_2),
    .reset(display_driver_rev2_13_reset_2), .reset_2(display_driver_rev2_14_reset_2));  // open: is_0, add_for_button_driver

  // Notes on the sheet:
  //   circle numbers
  //   memory init
  //   main
  //   computer
  //   human
  //   contents of rom_1 (hex, n*v repeats v):
  //   cc f0 d0 f d1 20 a1 d1 d d2 0 d3 4 5 e4 15 ab 8e 89 ee d d0 0 d1 6 a4 d1 d a4 d0 1 d1 10 d2 6 a e4
  //   2c a4 8a 8c 8d ee 23 8c d2 6 a e4 38 a4 8a 8c 8d ee 2f d0 f d1 0 a1 d0 1e d1 3 a1 d0 1 ee f7 177*0
  //   d1 ff a4 ee
  //   contents of rom_2 (hex, n*v repeats v):
  //   ee 47 d0 f d1 2 a1 d0 d 0 e4 22 d1 10 11 b5 d2 10 59 c0 b0 d2 fe a8 d2 fc a9 d1 0 a9 c4 88 ee 9 d0 f
  //   d1 0 a1 d7 d0 fb b0 0 e1 41 d0 1e b0 88 88 0 e1 3a d1 3 ee 3c d1 2 d0 1e a1 ee 46 d0 fb d1 0 a1 d7
  //   d0 e b0 d6 2 d6 28 d0 f8 b0 0 e0 5a d0 f d1 10 a1 d4 d0 1e b0 ee f7 152*0 d1 ff a4 ee
  //   contents of rom_3 (hex, n*v repeats v):
  //   d1 fa b5 d0 7 41 d0 6 34 e4 d ee 0 d0 7 11 b6 a e1 16 ee 0 d0 10 11 b5 d0 1f a1 d0 4 ee f7 214*0 d1
  //   ff a4 ee
  //   contents of rom_4 (hex, n*v repeats v):
  //   d0 f d1 8 a1 d0 f9 b1 5 e1 e b1 ee 8 6 8a ba a e1 20 d0 f d1 41 a1 d0 f d1 0 a1 ee 0 d0 1f a1 d0 f
  //   d1 40 a1 d0 f d1 0 d0 4 ee f7 199*0 d1 ff a4 ee 0 d4
  //   contents of rom_5 (hex, n*v repeats v):
  //   ee d2 d2 fb d3 1 ab d7 d3 1e bf 8b 8b f e1 14 d3 6 ee 16 d3 d d7 d0 f d1 4 a1 d0 1f b1 5 e1 25 b1 ee
  //   1f d0 10 b2 36 e0 2f 8c b2 ee 28 d3 10 33 c b1 d2 0 a2 5 e0 4e 8c d6 8 33 e1 41 8c d3 e 33 e4 48 d0
  //   0 b2 8e a2 89 ee 37 d1 1e b5 89 89 c1 5 e1 5b d2 d ee 5d d2 6 32 e1 65 d6 2 c7 ee c7 c7 d1 7 31 f e1
  //   77 5 e4 73 d2 1 ee 75 d2 0 ee 80 5 e5 7e d2 1 ee 80 d2 0 a e0 85 d6 2 1 b5 d2 1 36 e1 c7 d1 1e b5 d2
  //   2 36 e1 a3 d1 6 31 d2 0 5 e0 a1 8a 8a 89 ee 99 ee ae d2 c 3 f e0 ae 8a 8a 8b ee a6 1 19 d3 0 a3 b6
  //   8e a7 d1 1e b5 d0 2 31 e1 c2 d1 d ee c4 d1 6 b4 18 a4 d0 1f d1 0 a1 d0 f d1 0 a1 d7 d6 17 d0 1 ee f7
  //   31*0 d1 ff a4 ee
endmodule

module ext_register (
  input  [7:0] register_addres,
  input  [7:0] cpu_mem_addr_in,
  input  r_w_prime,
  input  data_flag_in,
  input  [7:0] IO_in,
  input  cl,
  input  reset,
  output cl_2,
  output reset_2,
  output [7:0] IO_out,
  output r_w_prime_out,
  output [7:0] cpu_mem_addr_out,
  output data_flag_out,
  output [7:0] data_out
);

  wire and_1_out, comparator_1_eq, not_1_out;

  Comparator comparator_1 (.a(cpu_mem_addr_in), .b(register_addres), .eq(comparator_1_eq));  // open: gt, lt
  not not_1 (not_1_out, r_w_prime);
  and and_1 (and_1_out, comparator_1_eq, data_flag_in, not_1_out);
  Register register_1 (.D(IO_in), .en(and_1_out), .Q(data_out), .clk(cl), .clr(reset));

  assign cl_2 = cl;
  assign cpu_mem_addr_out = cpu_mem_addr_in;
  assign data_flag_out = data_flag_in;
  assign IO_out = IO_in;
  assign r_w_prime_out = r_w_prime;
  assign reset_2 = reset;
endmodule
