// Logisim project project_workings.circ as structural Verilog: 10 circuits, main circuit main
module main (
  input  [7:0] in_1,
  input  [7:0] in_2,
  input  in_3,
  input  [7:0] in_4,
  input  [3:0] in_5,
  input  [7:0] in_6,
  input  in_7,
  output [3:0] out_8,
  output [3:0] out_9
);

  wire button_1_out, button_2_out, button_3_out, button_4_out, button_5_out, button_6_out,
       button_driver_1_trigger, clock_1_out, clock_2_out, display_driver_1_cl_2, display_driver_1_r_w_2,
       display_driver_rev2_1_cl_2, display_driver_rev2_1_r_w_2, display_driver_rev2_1_reset_2,
       display_driver_rev2_2_p10, display_driver_rev2_2_p11, display_driver_rev2_2_p12,
       display_driver_rev2_2_p13, display_driver_rev2_2_p14, display_driver_rev2_2_p15,
       display_driver_rev2_2_p16, display_driver_rev2_3_p15, display_driver_rev2_3_p16,
       display_driver_rev2_3_p17;
  wire [3:0] bin_to_bcd_converter_1_out_2, bin_to_bcd_converter_1_out_3, button_driver_2_addr_2,
       button_driver_4_addr_2, button_driver_5_addr_2, button_driver_6_addr_2, display_driver_1_bcd_1,
       display_driver_1_bcd_2, display_driver_2_bcd_1, display_driver_2_bcd_2,
       display_driver_rev2_1_add_for_button_driver, display_driver_rev2_1_addr_out,
       display_driver_rev2_1_addr_out_chain, display_driver_rev2_1_bcd_1, display_driver_rev2_1_bcd_2,
       display_driver_rev2_2_p7, display_driver_rev2_2_p8, display_driver_rev2_2_p9,
       display_driver_rev2_3_p8, display_driver_rev2_3_p9, display_driver_rev2_3_p10,
       display_driver_rev2_3_p12, display_driver_rev2_3_p13, display_driver_rev2_3_p18,
       display_driver_rev2_4_add_for_button_driver, display_driver_rev2_4_bcd_1;
  wire [7:0] display_driver_1_addr_out, display_driver_1_data_2, display_driver_1_data_read_2,
       display_driver_2_data_read_2, display_driver_rev2_1_data_out, display_driver_rev2_3_p14,
       display_driver_rev2_4_data_out;

  // Probe on in_6
  // Probe on in_1
  LED led_1 (.in(button_driver_1_trigger));
  LED led_2 (.in(display_driver_rev2_2_p10));
  // Probe on in_5
  Clock clock_1 (.out(clock_1_out));
  button_driver button_driver_1 (
    .addr_2(out_8), .button(button_1_out), .trigger(button_driver_1_trigger), .addr(button_driver_2_addr_2));  // open: pos
  Button button_1 (.out(button_1_out));
  WLD wld_1 (
    .in_3(display_driver_rev2_2_p10), .des(display_driver_rev2_1_bcd_1), .ed(display_driver_rev2_1_bcd_2));  // open: win, lose
  Hex_Digit_Display hex_digit_display_1 (.value(display_driver_rev2_1_bcd_1));  // open: dp
  bin_to_bcd_converter bin_to_bcd_converter_1 (
    .in_1(in_1), .out_2(bin_to_bcd_converter_1_out_2), .out_3(bin_to_bcd_converter_1_out_3));
  button_driver button_driver_2 (
    .addr_2(button_driver_2_addr_2), .button(button_2_out), .trigger(button_driver_1_trigger), .addr(4'b0000));  // open: pos
  Button button_2 (.out(button_2_out));
  Hex_Digit_Display hex_digit_display_2 (.value(display_driver_rev2_1_bcd_2));  // open: dp
  button_driver button_driver_3 (
    .addr_2(out_9), .pos(display_driver_rev2_1_add_for_button_driver), .button(button_3_out),
    .addr(button_driver_4_addr_2));  // open: trigger
  Button button_3 (.out(button_3_out));
  Hex_Digit_Display hex_digit_display_3 (.value(bin_to_bcd_converter_1_out_2));  // open: dp
  Pull_Resistor #(.pull(1)) pull_resistor_1 (.node(button_driver_1_trigger));
  Hex_Digit_Display hex_digit_display_4 (.value(display_driver_rev2_2_p8));  // open: dp
  Hex_Digit_Display hex_digit_display_5 (.value(display_driver_rev2_2_p7));  // open: dp
  display_driver_rev2 display_driver_rev2_1 (
    .addr_in(in_5), .addr_in_chain(4'b0000), .data(in_6), .cl(clock_1_out),
    .addr_out(display_driver_rev2_1_addr_out), .addr_out_chain(display_driver_rev2_1_addr_out_chain),
    .data_out(display_driver_rev2_1_data_out), .cl_2(display_driver_rev2_1_cl_2),
    .bcd_1(display_driver_rev2_1_bcd_1), .bcd_2(display_driver_rev2_1_bcd_2), .r_w(in_7),
    .r_w_2(display_driver_rev2_1_r_w_2), .reset(1'b0), .reset_2(display_driver_rev2_1_reset_2),
    .add_for_button_driver(display_driver_rev2_1_add_for_button_driver));  // open: is_0
  Button button_4 (.out(button_4_out));
  Hex_Digit_Display hex_digit_display_6 (.value(bin_to_bcd_converter_1_out_3));  // open: dp
  // display_driver_rev2 display_driver_rev2_2: pin names not known; wires that end beside it: display_driver_rev2_1_addr_out, display_driver_rev2_1_addr_out_chain, display_driver_rev2_1_data_out, display_driver_rev2_1_cl_2, display_driver_rev2_1_r_w_2, display_driver_rev2_1_reset_2, display_driver_rev2_2_p7, display_driver_rev2_2_p8, display_driver_rev2_2_p9, display_driver_rev2_2_p10, display_driver_rev2_2_p11, display_driver_rev2_2_p12, display_driver_rev2_2_p13, display_driver_rev2_2_p14, display_driver_rev2_2_p15, display_driver_rev2_2_p16
  button_driver button_driver_4 (
    .addr_2(button_driver_4_addr_2), .pos(display_driver_rev2_2_p9), .button(button_4_out),
    .addr(button_driver_5_addr_2));  // open: trigger
  Hex_Digit_Display hex_digit_display_7 (.value(display_driver_rev2_3_p8));  // open: dp
  Hex_Digit_Display hex_digit_display_8 (.value(display_driver_rev2_3_p9));  // open: dp
  button_driver button_driver_5 (
    .addr_2(button_driver_5_addr_2), .pos(display_driver_rev2_3_p10), .button(button_5_out),
    .addr(button_driver_6_addr_2));  // open: trigger
  Button button_5 (.out(button_5_out));
  Pull_Resistor #(.pull(1)) pull_resistor_2 (.node(display_driver_rev2_2_p10));
  Hex_Digit_Display hex_digit_display_9 (.value(display_driver_rev2_4_bcd_1));  // open: dp
  // display_driver_rev2 display_driver_rev2_3: pin names not known; wires that end beside it: display_driver_rev2_2_p10, display_driver_rev2_2_p11, display_driver_rev2_2_p12, display_driver_rev2_2_p13, display_driver_rev2_2_p14, display_driver_rev2_2_p15, display_driver_rev2_2_p16, display_driver_rev2_3_p8, display_driver_rev2_3_p9, display_driver_rev2_3_p10, display_driver_rev2_2_p10, display_driver_rev2_3_p12, display_driver_rev2_3_p13, display_driver_rev2_3_p14, display_driver_rev2_3_p15, display_driver_rev2_3_p16, display_driver_rev2_3_p17, display_driver_rev2_3_p18
  WLD wld_2 ();  // open: in_3, des, ed, win, lose
  Hex_Digit_Display hex_digit_display_10 (.value(display_driver_rev2_3_p18));  // open: dp
  button_driver button_driver_6 (
    .addr_2(button_driver_6_addr_2), .pos(display_driver_rev2_4_add_for_button_driver), .button(button_6_out));  // open: trigger, addr
  Button button_6 (.out(button_6_out));
  // Probe on in_2
  // Probe on in_4
  // Probe on display_driver_1_data_read_2
  display_driver_rev2 display_driver_rev2_4 (
    .addr_in(display_driver_rev2_3_p12), .addr_in_chain(display_driver_rev2_3_p13),
    .data(display_driver_rev2_3_p14), .cl(display_driver_rev2_3_p15),
    .data_out(display_driver_rev2_4_data_out), .bcd_1(display_driver_rev2_4_bcd_1),
    .bcd_2(display_driver_rev2_3_p18), .is_0(display_driver_rev2_2_p10), .r_w(display_driver_rev2_3_p16),
    .reset(display_driver_rev2_3_p17), .add_for_button_driver(display_driver_rev2_4_add_for_button_driver));  // open: addr_out, addr_out_chain, cl_2, r_w_2, reset_2
  // Probe on display_driver_rev2_4_data_out
  Clock clock_2 (.out(clock_2_out));
  Hex_Digit_Display hex_digit_display_11 (.value(display_driver_1_bcd_1));  // open: dp
  Hex_Digit_Display hex_digit_display_12 (.value(display_driver_1_bcd_2));  // open: dp
  display_driver display_driver_1 (
    .cl(clock_2_out), .r_w(in_3), .addr_in(in_2), .data(in_4), .cl_2(display_driver_1_cl_2),
    .r_w_2(display_driver_1_r_w_2), .addr_out(display_driver_1_addr_out), .bcd_1(display_driver_1_bcd_1),
    .bcd_2(display_driver_1_bcd_2), .data_2(display_driver_1_data_2),
    .data_read(display_driver_2_data_read_2), .data_read_2(display_driver_1_data_read_2));
  Hex_Digit_Display hex_digit_display_13 (.value(display_driver_2_bcd_1));  // open: dp
  Hex_Digit_Display hex_digit_display_14 (.value(display_driver_2_bcd_2));  // open: dp
  display_driver display_driver_2 (
    .cl(display_driver_1_cl_2), .r_w(display_driver_1_r_w_2), .addr_in(display_driver_1_addr_out),
    .data(display_driver_1_data_2), .bcd_1(display_driver_2_bcd_1), .bcd_2(display_driver_2_bcd_2),
    .data_read_2(display_driver_2_data_read_2));  // open: cl_2, r_w_2, addr_out, data_2, data_read
endmodule

module bin_to_bcd_converter (
  input  [7:0] in_1,
  output [3:0] out_2,
  output [3:0] out_3
);

  ROM rom_1 (.addr(in_1), .data({out_2, out_3}), .sel(1'b1));

  // Notes on the sheet:
  //   contents of rom_1 (hex, n*v repeats v):
  //   0 1 2 3 4 5 6 7 8 9 10 11 12 13 14 15 16 17 18 19 20 21 22 23 24 25 26 27 28 29 30 31 32 33 34 35 36
  //   37 38 39 40 41 42 43 44 45 46 47 48 49 50 51 52 53 54 55 56 57 58 59 60 61 62 63 64 65 66 67 68 69
  //   70 71 72 73 74 75 76 77 78 79 80 81 82 83 84 85 86 87 88 89 90 91 92 93 94 95 96 97 98 99
endmodule

module display_driver (
  input  cl,
  input  r_w,
  input  [7:0] addr_in,
  input  [7:0] data,
  input  [7:0] data_read,
  output cl_2,
  output r_w_2,
  output [7:0] addr_out,
  output [3:0] bcd_1,
  output [3:0] bcd_2,
  output [7:0] data_2,
  output [7:0] data_read_2
);

  wire and_1_out, comparator_1_eq, not_1_out;
  wire [7:0] and_2_out, register_1_q;
  wire [7:7] and_3_out;

  Subtractor subtractor_1 (.a(addr_in), .b(8'h1), .out(addr_out));  // open: bin, bout
  Comparator comparator_1 (.a(addr_out), .b({8{1'b0}}), .eq(comparator_1_eq));  // open: gt, lt
  assign data_read_2 = and_2_out | data_read;  // OR_Gate or_1, 8 bits wide
  and and_1 (and_1_out, r_w, comparator_1_eq);
  Register register_1 (.D(data), .en(and_1_out), .Q(register_1_q), .clk(cl), .clr(1'b0));
  assign and_2_out = {8{and_3_out[7]}} & register_1_q;  // AND_Gate and_2, 8 bits wide
  Pull_Resistor pull_resistor_1 (.node(data_read));
  not not_1 (not_1_out, r_w);
  and and_3 (and_3_out[7], not_1_out, comparator_1_eq);
  bin_to_bcd_converter bin_to_bcd_converter_1 (.in_1(register_1_q), .out_2(bcd_1), .out_3(bcd_2));

  assign cl_2 = cl;
  assign data_2 = data;
  assign r_w_2 = r_w;
endmodule

module button_driver (
  input  [3:0] pos,
  input  [3:0] addr,
  input  button,
  output [3:0] addr_2,
  output trigger
);

  wire not_1_out;

  assign addr_2 = button ? pos : 4'bz;  // Controlled_Buffer controlled_buffer_1
  assign addr_2 = not_1_out ? addr : 4'bz;  // Controlled_Buffer controlled_buffer_2
  not not_1 (not_1_out, button);
  Transistor #(.\type ("n")) transistor_1 (.in(1'b0), .out(trigger), .gate(button));
  Pull_Resistor pull_resistor_1 (.node(addr));
endmodule

module display_driver_rev2 (
  input  r_w,
  input  [3:0] addr_in,
  input  [3:0] addr_in_chain,
  input  [7:0] data,
  input  cl,
  input  reset,
  output r_w_2,
  output [3:0] addr_out,
  output [3:0] addr_out_chain,
  output [7:0] data_out,
  output cl_2,
  output [3:0] bcd_1,
  output [3:0] bcd_2,
  output is_0,
  output reset_2,
  output [3:0] add_for_button_driver
);

  wire and_1_out, and_3_out, comparator_1_gt, comparator_1_lt, not_1_out, or_1_out;
  wire [7:0] and_2_out, \buf ;
  wire [7:7] our_addr;

  not not_1 (not_1_out, r_w);
  and and_1 (and_1_out, not_1_out, our_addr[7]);
  assign and_2_out = data & {8{our_addr[7]}};  // AND_Gate and_2, 8 bits wide
  and and_3 (and_3_out, our_addr[7], r_w);
  incrementer incrementer_1 (.in_1(addr_in_chain), .out_2(add_for_button_driver));
  Register register_1 (.D(and_2_out), .en(and_3_out), .Q(\buf ), .clk(cl), .clr(reset));
  MUX mux_1 (.Input_0(data), .sel(and_1_out), .Input_1(\buf ), .Output(data_out));
  Comparator comparator_1 (.a(\buf ), .b({8{1'b0}}), .gt(comparator_1_gt), .lt(comparator_1_lt));  // open: eq
  or or_1 (or_1_out, comparator_1_gt, comparator_1_lt);
  Comparator #(.width(4)) comparator_2 (.a(addr_in), .b(add_for_button_driver), .eq(our_addr[7]));  // open: gt, lt
  bin_to_bcd_converter bin_to_bcd_converter_1 (.in_1(\buf ), .out_2(bcd_1), .out_3(bcd_2));
  Transistor #(.\type ("n")) transistor_1 (.in(1'b0), .out(is_0), .gate(or_1_out));

  assign addr_out = addr_in;
  assign addr_out_chain = add_for_button_driver;
  assign cl_2 = cl;
  assign r_w_2 = r_w;
  assign reset_2 = reset;

  // Other names for the same wires on the sheet: addr[3:0] = addr_in; our_add_in_chain[3:0] = add_for_button_driver;
  //   our_addr[6:0] = {7{our_addr[7]}}; our_addr_1 = our_addr[7]; rw = r_w
endmodule

module incrementer (
  input  [3:0] in_1,
  output [3:0] out_2
);

  Adder #(.width(4)) adder_1 (.a(in_1), .b(4'b0001), .out(out_2), .cin(1'b0));  // open: cout
endmodule

module _4bit_to_8 (
  input  [3:0] in_1,
  output [7:0] out_2
);


  assign out_2 = {4'b0000, in_1};
endmodule

module bcd_to_bin (
  input  [3:0] des,
  input  [3:0] ed,
  output [7:0] \output 
);

  wire [7:0] multiplier_1_out, n4bit_to_8_1_out_2, n4bit_to_8_2_out_2;

  // Probe on ed
  // Probe on des
  _4bit_to_8 u_4bit_to_8_1 (.in_1(des), .out_2(n4bit_to_8_1_out_2));
  _4bit_to_8 u_4bit_to_8_2 (.in_1(ed), .out_2(n4bit_to_8_2_out_2));
  Multiplier multiplier_1 (.a(n4bit_to_8_1_out_2), .b(8'ha), .out(multiplier_1_out));  // open: cin, cout
  // Probe on \output 
  Adder adder_1 (.a(multiplier_1_out), .b(n4bit_to_8_2_out_2), .out(\output ));  // open: cin, cout
endmodule

module MUX (
  input  [7:0] Input_0,
  input  sel,
  input  [7:0] Input_1,
  output [7:0] Output
);

  wire [7:0] and_1_out, and_2_out;
  wire [7:7] not_1_out;

  not not_1 (not_1_out[7], sel);
  assign and_1_out = Input_0 & {8{not_1_out[7]}};  // AND_Gate and_1, 8 bits wide
  assign and_2_out = {8{sel}} & Input_1;  // AND_Gate and_2, 8 bits wide
  assign Output = and_1_out | and_2_out;  // OR_Gate or_1, 8 bits wide
endmodule

module WLD (
  input  [3:0] des,
  input  [3:0] ed,
  input  in_3,
  output win,
  output lose
);

  wire and_1_out, and_2_out, comparator_1_eq, comparator_1_lt, comparator_2_gt, comparator_2_lt, or_1_out,
       or_2_out;
  wire [7:0] bcd_to_bin_1_output, opVal;

  Subtractor subtractor_1 (.a(8'h30), .b(bcd_to_bin_1_output), .out(opVal), .bin(1'b0));  // open: bout
  // Probe on opVal
  bcd_to_bin bcd_to_bin_1 (.des(des), .ed(ed), .\output (bcd_to_bin_1_output));
  Comparator #(.mode("unsigned")) comparator_1 (
    .a(8'h18), .b(bcd_to_bin_1_output), .eq(comparator_1_eq), .lt(comparator_1_lt));  // open: gt
  Comparator #(.mode("unsigned")) comparator_2 (
    .a(bcd_to_bin_1_output), .b(opVal), .gt(comparator_2_gt), .lt(comparator_2_lt));  // open: eq
  or or_1 (or_1_out, comparator_1_eq, comparator_1_lt);
  and and_1 (and_1_out, in_3, comparator_2_gt);
  and and_2 (and_2_out, comparator_2_lt, in_3);
  or or_2 (or_2_out, or_1_out, and_1_out);
  Transistor #(.\type ("n")) transistor_1 (.in(1'b1), .out(lose), .gate(and_2_out));
  Transistor #(.\type ("n")) transistor_2 (.in(1'b1), .out(win), .gate(or_2_out));

  // Notes on the sheet:
  //   win
  //   win
  //   lose
endmodule
